# Fritzing sketch assignment (saved by Fritzing 0.9.3b)
breadboards: 1

parts:
  Arduino_+_Wifi_Shield = Arduino Uno (Rev3)
  LCD = LCD screen
  Potentiometer = Trimmer Potentiometer [maximum_resistance=10kΩ package=THT]
  Resistor = Resistor [tolerance=±5% resistance=220 package=THT]
  T1 = LM35 Temperature Sensor [package="TO92 [THT]"]
  R3 = PHOTOCELL [package=photocell-kit]
  Resistor_2 = Resistor [tolerance=±5% resistance=220 package=THT]

nets:
  N1: Arduino_+_Wifi_Shield.A0, R3.P$2, Resistor_2.Pin_0
  N2: Arduino_+_Wifi_Shield.A1, T1.Vout
  N3: Arduino_+_Wifi_Shield.D8, LCD.DB6
  N4: Arduino_+_Wifi_Shield.D9_PWM, LCD.DB7
  GND: Arduino_+_Wifi_Shield.GND, LCD.VSS, LCD.R/W, LCD.LED-, Potentiometer.leg1, T1.GND, Resistor_2.Pin_1
  N5: Arduino_+_Wifi_Shield.D2, LCD.RS
  N6: Arduino_+_Wifi_Shield.D3_PWM, LCD.E
  N7: Arduino_+_Wifi_Shield.D5_PWM, LCD.DB4
  N8: Arduino_+_Wifi_Shield.D6_PWM, LCD.DB5
  5V: Arduino_+_Wifi_Shield.5V, LCD.VDD, Potentiometer.leg2, Resistor.Pin_1, T1.+Vs, R3.P$1
  N9: LCD.V0, Potentiometer.wiper
  N10: LCD.LED+, Resistor.Pin_0
